// Logisim project cpu.circ as structural Verilog: 7 circuits, main circuit cpu
module cpu (
);

  wire CLK, controller_1_p1, controller_1_p5, controller_1_p7, controller_1_p8, controller_1_p9,
       controller_1_p11, controller_1_p13, controller_1_p14, controller_1_p15, eq, RST;
  wire [1:0] controller_1_p2, controller_1_p10, controller_1_p12, controller_1_p16;
  wire [3:0] controller_1_p6;
  wire [4:0] decoder_1_out_2, decoder_1_out_4, decoder_1_out_6, decoder_1_out_8, multiplexer_1_out,
       multiplexer_3_out, multiplexer_4_out;
  wire [5:0] controller_1_p3, controller_1_p4;
  wire [15:0] decoder_1_out_9, \总周期数 , \无条件分支指令数 , \有条件分支成功跳转 , \有条件分支指令数 ;
  wire [23:0] divider1_1_out_2, divider_1_out_2;
  wire [25:0] decoder_1_out_5;
  wire [31:0] alu_1_result, extender_1_out_3, extender_1_out_4, mips_ram_1_p8, multiplexer_2_out,
       multiplexer_5_out, multiplexer_6_out, npc_1_out_8, npc_1_out_9, PC_q, registerfile_1_p7,
       registerfile_1_p8, rom_1_data, SyscallOut;

  Button \u_总复位  (.out(RST));
  NPC npc_1 (
    .in_2(PC_q), .out_8(npc_1_out_8), .in_6(decoder_1_out_5), .in_1(decoder_1_out_9),
    .in_4(registerfile_1_p7), .in_5(controller_1_p2), .out_9(npc_1_out_9), .in_3(eq), .in_7(alu_1_result));
  Register #(.width(32)) PC (.D(npc_1_out_8), .en(controller_1_p1), .Q(PC_q), .clk(CLK), .clr(RST));
  Divider divider_1 (.in_1(PC_q), .out_2(divider_1_out_2));
  Hex_Digit_Display hex_digit_display_1 (.value(SyscallOut[31:28]));  // open: dp
  Hex_Digit_Display hex_digit_display_2 (.value(SyscallOut[27:24]));  // open: dp
  Clock clock_1 (.out(CLK));
  Hex_Digit_Display hex_digit_display_3 (.value(SyscallOut[23:20]));  // open: dp
  Hex_Digit_Display hex_digit_display_4 (.value(SyscallOut[19:16]));  // open: dp
  Hex_Digit_Display hex_digit_display_5 (.value(SyscallOut[11:8]));  // open: dp
  Hex_Digit_Display hex_digit_display_6 (.value(SyscallOut[15:12]));  // open: dp
  // Controller controller_1: pin names not known; wires that end beside it: controller_1_p1, controller_1_p2, controller_1_p3, controller_1_p4, controller_1_p5, controller_1_p6, controller_1_p7, controller_1_p8, controller_1_p9, controller_1_p10, controller_1_p11, controller_1_p12, controller_1_p13, controller_1_p14, controller_1_p15, controller_1_p16
  Decoder decoder_1 (
    .out_2(decoder_1_out_2), .out_3(controller_1_p3), .out_4(decoder_1_out_4), .out_5(decoder_1_out_5),
    .in_1(rom_1_data), .out_6(decoder_1_out_6), .out_7(controller_1_p4), .out_8(decoder_1_out_8),
    .out_9(decoder_1_out_9));
  ROM #(.addrWidth(24), .dataWidth(32)) rom_1 (.addr(divider_1_out_2), .data(rom_1_data));  // open: sel
  Hex_Digit_Display hex_digit_display_7 (.value(SyscallOut[7:4]));  // open: dp
  Hex_Digit_Display hex_digit_display_8 (.value(SyscallOut[3:0]));  // open: dp
  Multiplexer #(.select(2), .width(5), .disabled(0), .enable("false")) multiplexer_1 (
    .in0(decoder_1_out_8), .in1(decoder_1_out_6), .in2({5{1'b1}}), .out(multiplexer_1_out),
    .sel(controller_1_p16));  // open: in3
  Multiplexer #(.select(2), .width(32), .disabled(0), .enable("false")) multiplexer_2 (
    .in0(alu_1_result), .in1(npc_1_out_9), .in2(mips_ram_1_p8), .out(multiplexer_2_out),
    .sel(controller_1_p12));  // open: in3
  Multiplexer #(.width(5), .disabled(0), .enable("false")) multiplexer_3 (
    .in0(decoder_1_out_6), .in1(5'b00100), .out(multiplexer_3_out), .sel(controller_1_p15));
  Multiplexer #(.width(5), .disabled(0), .enable("false")) multiplexer_4 (
    .in0(decoder_1_out_4), .in1(5'b00010), .out(multiplexer_4_out), .sel(controller_1_p14));
  // Probe on \总周期数 
  // Probe on \无条件分支指令数 
  // Probe on \有条件分支指令数 
  // Probe on \有条件分支成功跳转 
  // RegisterFile registerfile_1: pin names not known; wires that end beside it: multiplexer_2_out, CLK, controller_1_p13, multiplexer_1_out, multiplexer_4_out, multiplexer_3_out, registerfile_1_p7, registerfile_1_p8
  Extender extender_1 (
    .in_1(decoder_1_out_2), .out_3(extender_1_out_3), .out_4(extender_1_out_4), .in_2(decoder_1_out_9));
  Multiplexer #(.width(32), .disabled(0), .enable("false")) multiplexer_5 (
    .in0(registerfile_1_p7), .in1(registerfile_1_p8), .out(multiplexer_5_out), .sel(controller_1_p11));
  ALU alu_1 (
    .AluOP(controller_1_p6), .X(multiplexer_5_out), .Equal(eq), .Result(alu_1_result), .Y(multiplexer_6_out));  // open: Signed_Overflow, Result_2, UnSigned_Overflow
  Multiplexer #(.select(2), .width(32), .disabled(0), .enable("false")) multiplexer_6 (
    .in0(registerfile_1_p8), .in1(extender_1_out_3), .in2(extender_1_out_4), .in3(32'ha),
    .out(multiplexer_6_out), .sel(controller_1_p10));
  Register #(.width(32)) register_1 (.D(registerfile_1_p8), .en(controller_1_p5), .Q(SyscallOut), .clk(CLK), .clr(RST));
  Divider1 divider1_1 (.in_1(alu_1_result), .out_2(divider1_1_out_2));
  // MIPS_RAM mips_ram_1: pin names not known; wires that end beside it: divider1_1_out_2, registerfile_1_p8, controller_1_p7, controller_1_p8, CLK, controller_1_p9, RST, mips_ram_1_p8

  // Notes on the sheet:
  //   数码管输出应该用寄存器锁存，否则显示数据只能一闪而过
  //   可以通过项目增加Logisim库的方式将前几次实验完成的电路作为子电路引入到本电路中使用
  //   数码管输出
  //   总复位信号应将除ROM以外所有存储组件全部清零
endmodule

module Controller (
  input  [5:0] in_1,
  input  [5:0] in_2,
  output out_3,
  output [3:0] out_4,
  output out_5,
  output [1:0] out_6,
  output [1:0] out_7,
  output out_8,
  output out_9,
  output [1:0] out_10,
  output [3:0] out_11,
  output out_12,
  output out_13,
  output [1:0] out_14,
  output out_15,
  output out_16
);

  wire add, addi, addiu, adds, addu, \and , andi, ands, beq, bltz, bne, bs, cmps, comparator_1_eq,
       comparator_16_eq, comparator_17_eq, comparator_18_eq, comparator_19_eq, comparator_20_eq,
       comparator_21_eq, comparator_22_eq, comparator_23_eq, comparator_24_eq, comparator_25_eq,
       comparator_26_eq, comparator_27_eq, comparator_28_eq, comparator_29_eq, j, jal, jr, js, \nor , \or ,
       or_7_out, or_9_out, ori, ors, rlshifters, sb, sll, slt, slti, sltu, sra, srl, srlv, sub, sw, xori;

  Comparator #(.width(6)) comparator_1 (.a(in_1), .b({6{1'b0}}), .eq(comparator_1_eq));  // open: gt, lt
  Comparator #(.width(6)) comparator_2 (.a(in_1), .b(6'b001000), .eq(addi));  // open: gt, lt
  Comparator #(.width(6)) comparator_3 (.a(in_1), .b(6'b001001), .eq(addiu));  // open: gt, lt
  Comparator #(.width(6)) comparator_4 (.a(in_1), .b(6'b001100), .eq(andi));  // open: gt, lt
  Comparator #(.width(6)) comparator_5 (.a(in_1), .b(6'b001101), .eq(ori));  // open: gt, lt
  Comparator #(.width(6)) comparator_6 (.a(in_1), .b(6'b001110), .eq(xori));  // open: gt, lt
  Comparator #(.width(6)) comparator_7 (.a(in_1), .b(6'b001010), .eq(slti));  // open: gt, lt
  Comparator #(.width(6)) comparator_8 (.a(in_1), .b(6'b100011), .eq(out_12));  // open: gt, lt
  Comparator #(.width(6)) comparator_9 (.a(in_1), .b(6'b101011), .eq(sw));  // open: gt, lt
  Comparator #(.width(6)) comparator_10 (.a(in_1), .b(6'b101000), .eq(sb));  // open: gt, lt
  Comparator #(.width(6)) comparator_11 (.a(in_1), .b(6'b000100), .eq(beq));  // open: gt, lt
  Comparator #(.width(6)) comparator_12 (.a(in_1), .b(6'b000101), .eq(bne));  // open: gt, lt
  Comparator #(.width(6)) comparator_13 (.a(in_1), .b(6'b000001), .eq(bltz));  // open: gt, lt
  Comparator #(.width(6)) comparator_14 (.a(in_1), .b(6'b000010), .eq(j));  // open: gt, lt
  Comparator #(.width(6)) comparator_15 (.a(in_1), .b(6'b000011), .eq(jal));  // open: gt, lt
  Comparator #(.width(6)) comparator_16 (.a(in_2), .b(6'b100000), .eq(comparator_16_eq));  // open: gt, lt
  Comparator #(.width(6)) comparator_17 (.a(in_2), .b(6'b100001), .eq(comparator_17_eq));  // open: gt, lt
  Comparator #(.width(6)) comparator_18 (.a(in_2), .b(6'b100100), .eq(comparator_18_eq));  // open: gt, lt
  Comparator #(.width(6)) comparator_19 (.a(in_2), .b(6'b100010), .eq(comparator_19_eq));  // open: gt, lt
  Comparator #(.width(6)) comparator_20 (.a(in_2), .b(6'b100101), .eq(comparator_20_eq));  // open: gt, lt
  Comparator #(.width(6)) comparator_21 (.a(in_2), .b(6'b100111), .eq(comparator_21_eq));  // open: gt, lt
  Comparator #(.width(6)) comparator_22 (.a(in_2), .b(6'b000101), .eq(comparator_22_eq));  // open: gt, lt
  Comparator #(.width(6)) comparator_23 (.a(in_2), .b(6'b101010), .eq(comparator_23_eq));  // open: gt, lt
  Comparator #(.width(6)) comparator_24 (.a(in_2), .b(6'b101011), .eq(comparator_24_eq));  // open: gt, lt
  Comparator #(.width(6)) comparator_25 (.a(in_2), .b({6{1'b0}}), .eq(comparator_25_eq));  // open: gt, lt
  Comparator #(.width(6)) comparator_26 (.a(in_2), .b(6'b000011), .eq(comparator_26_eq));  // open: gt, lt
  Comparator #(.width(6)) comparator_27 (.a(in_2), .b(6'b000010), .eq(comparator_27_eq));  // open: gt, lt
  Comparator #(.width(6)) comparator_28 (.a(in_2), .b(6'b001000), .eq(comparator_28_eq));  // open: gt, lt
  Comparator #(.width(6)) comparator_29 (.a(in_2), .b(6'b001100), .eq(comparator_29_eq));  // open: gt, lt
  and and_1 (add, comparator_1_eq, comparator_16_eq);
  and and_2 (addu, comparator_1_eq, comparator_17_eq);
  and and_3 (\and , comparator_1_eq, comparator_18_eq);
  and and_4 (sub, comparator_1_eq, comparator_19_eq);
  and and_5 (\or , comparator_1_eq, comparator_20_eq);
  and and_6 (\nor , comparator_1_eq, comparator_21_eq);
  and and_7 (srlv, comparator_1_eq, comparator_22_eq);
  and and_8 (slt, comparator_1_eq, comparator_23_eq);
  and and_9 (sltu, comparator_1_eq, comparator_24_eq);
  and and_10 (sll, comparator_1_eq, comparator_25_eq);
  and and_11 (sra, comparator_1_eq, comparator_26_eq);
  and and_12 (srl, comparator_1_eq, comparator_27_eq);
  and and_13 (jr, comparator_1_eq, comparator_28_eq);
  and and_14 (out_5, comparator_1_eq, comparator_29_eq);
  or or_1 (cmps, slti, bltz, slt);
  or or_2 (ors, \or , ori);
  or or_3 (ands, \and , andi);
  or or_4 (adds, add, addi, addu, addiu);
  or or_5 (rlshifters, srlv, srl);
  or or_6 (out_3, sll, sra, srl);
  or or_7 (or_7_out, addi, addiu, andi, ori, xori, slti, out_12, sw, sb);
  Priority_Encoder #(.select(4)) priority_encoder_1 (
    .in0(1'b1), .in1(sra), .in2(rlshifters), .in3(1'b0), .in4(1'b0), .in5(adds), .in6(sub), .in7(ands),
    .in8(ors), .in9(xori), .in10(\nor ), .in11(cmps), .in12(sltu), .in13(1'b0), .in14(1'b0), .in15(1'b0),
    .out(out_11));  // open: gs, en_out, en_in
  Priority_Encoder #(.select(2)) priority_encoder_2 (
    .in0(1'b1), .in1(out_3), .in2(or_7_out), .in3(out_5), .out(out_7));  // open: gs, en_out, en_in
  not not_1 (out_4[2], sb);
  or or_8 (out_8, sw, sb);
  or or_9 (or_9_out, addi, addiu, andi, ori, xori, slti, out_12);
  Priority_Encoder #(.select(2)) priority_encoder_3 (
    .in0(1'b1), .in1(jal), .in2(out_12), .in3(1'b0), .out(out_14));  // open: gs, en_out, en_in
  nor nor_1 (out_15, sw, sb, beq, bne, bltz, j, jr, out_5);
  Priority_Encoder #(.select(2)) priority_encoder_4 (
    .in0(1'b1), .in1(or_9_out), .in2(jal), .in3(1'b0), .out(out_10));  // open: gs, en_out, en_in
  or or_10 (bs, bne, beq, bltz);
  or or_11 (js, j, jal);
  Priority_Encoder #(.select(2)) priority_encoder_5 (
    .in0(1'b1), .in1(bs), .in2(js), .in3(jr), .out(out_6));  // open: gs, en_out, en_in

  assign {out_4[3], out_4[1:0]} = {1'b1, {2{out_4[2]}}};
  assign out_9 = out_5;
  assign out_13 = out_5;
  assign out_16 = out_5;

  // Other names for the same wires on the sheet: ALUop[3:0] = out_11; CA = out_3; CB[1:0] = out_7; CPC[1:0] = out_6;
  //   Din[1:0] = out_14; funct[5:0] = in_2; ld = out_12; lw = out_12; op[5:0] = in_1; Rw[1:0] = out_10;
  //   Sel[2:0] = {3{out_4[2]}}; str = out_8; Ra = out_5; Rb = out_5; SysC1 = out_5; SysC2 = out_5; syscall = out_5;
  //   We = out_15
endmodule

module NPC (
  input  [15:0] in_1,
  input  [31:0] in_2,
  input  in_3,
  input  [31:0] in_4,
  input  [1:0] in_5,
  input  [25:0] in_6,
  input  [31:0] in_7,
  output [31:0] out_8,
  output [31:0] out_9
);

  wire [31:0] adder_2_out, and_1_out, bit_extender_1_out, bit_extender_2_out;

  Adder #(.width(32)) adder_1 (.a(in_2), .b(32'h4), .out(out_9));  // open: cin, cout
  assign and_1_out = in_2 & 32'hf0000000;  // AND_Gate and_1, 32 bits wide
  assign bit_extender_1_out = {{4{1'b0}}, {in_6, 2'b00}};  // Bit_Extender bit_extender_1
  assign bit_extender_2_out = {{16{1'b0}}, in_1};  // Bit_Extender bit_extender_2
  // OR_Gate or_1 has open pins: in0=and_1_out, in1=bit_extender_1_out, out=open
  Adder #(.width(32)) adder_2 (.a(bit_extender_2_out), .b(out_9), .out(adder_2_out));  // open: cin, cout
  Multiplexer #(.width(32), .disabled(0), .enable("false")) multiplexer_1 (.sel(in_3));  // open: in0, in1, out

  // Other names for the same wires on the sheet: label[25:0] = in_6; ALUout[31:0] = in_7; CNPC[1:0] = in_5; eq = in_3;
  //   IMM[15:0] = in_1; Input[31:0] = in_2; Output[31:0] = out_8; PC4[31:0] = out_9; RF1[31:0] = in_4
endmodule

module Divider (
  input  [31:0] in_1,
  output [23:0] out_2
);


  assign out_2 = in_1[25:2];

  // Other names for the same wires on the sheet: Input[31:0] = in_1; Output[23:0] = in_1[25:2]
endmodule

module Divider1 (
  input  [31:0] in_1,
  output [23:0] out_2
);


  assign out_2 = in_1[23:0];

  // Other names for the same wires on the sheet: Input[31:0] = in_1; Output[23:0] = in_1[23:0]
endmodule

module Decoder (
  input  [31:0] in_1,
  output [4:0] out_2,
  output [5:0] out_3,
  output [4:0] out_4,
  output [25:0] out_5,
  output [4:0] out_6,
  output [5:0] out_7,
  output [4:0] out_8,
  output [15:0] out_9
);


  assign out_2 = in_1[10:6];
  assign out_3 = in_1[31:26];
  assign out_4 = in_1[25:21];
  assign out_5 = in_1[25:0];
  assign out_6 = in_1[20:16];
  assign out_7 = in_1[5:0];
  assign out_8 = in_1[15:11];
  assign out_9 = in_1[15:0];

  // Other names for the same wires on the sheet: funct[5:0] = in_1[5:0]; IMM[15:0] = in_1[15:0]; Input[31:0] = in_1;
  //   label[25:0] = in_1[25:0]; s[4:0] = in_1[10:6]; rd[4:0] = in_1[15:11]; rt[4:0] = in_1[20:16];
  //   rs[4:0] = in_1[25:21]; op[5:0] = in_1[31:26]
endmodule

module Extender (
  input  [4:0] in_1,
  input  [15:0] in_2,
  output [31:0] out_3,
  output [31:0] out_4
);

  assign out_3 = {{27{1'b0}}, in_1};  // Bit_Extender bit_extender_1
  assign out_4 = {{16{1'b0}}, in_2};  // Bit_Extender bit_extender_2

  // Other names for the same wires on the sheet: eIMM[31:0] = out_4; es[31:0] = out_3; IMM[15:0] = in_2;
  //   s[4:0] = in_1
endmodule
